// Digital circuit mode_selector.dig as structural Verilog
module mode_selector (
  input  ID,
  input  PWD,
  input  DIS,
  input  RESET,
  input  CLK,
  input  RST,
  output IDO,
  output PWDO
);

  wire and_1_out, and_2_out, and_3_out, d_ff_1_nq, multiplexer_1_out, or_1_out;

  D_FF d_ff_1 (.D(PWD), .C(CLK), .nQ(d_ff_1_nq));  // open: Q
  and and_1 (and_1_out, PWD, d_ff_1_nq);
  or or_1 (or_1_out, and_1_out, ID);
  and and_2 (and_2_out, ~RESET, RST);  // And
  D_FF_AS d_ff_as_1 (.Set(1'b0), .D(multiplexer_1_out), .C(CLK), .Clr(~and_2_out), .Q(PWDO), .nQ(IDO));
  Multiplexer multiplexer_1 (.sel(and_3_out), .in_0(PWDO), .in_1(PWD), .out(multiplexer_1_out));
  and and_3 (and_3_out, or_1_out, ~DIS);  // And
endmodule
