// Digital circuit shifter.dig as structural Verilog
module shifter (
  input  [3:0] IN,
  input  EN,
  input  DA,
  input  CLK,
  input  RST,
  output [3:0] ID1,
  output [3:0] ID0,
  output [6:0] HEX
);

  wire add_1_c_o, and_1_out;
  wire [3:0] multiplexer_1_out, multiplexer_2_out;
  wire [4:3] or_1_out;

  and and_1 (and_1_out, DA, EN);
  D_FF_AS #(.Bits(4)) d_ff_as_1 (.Set(1'b0), .D(multiplexer_1_out), .C(CLK), .Clr(~RST), .Q(ID0));  // open: nQ
  Multiplexer #(.Bits(4)) multiplexer_1 (.sel(and_1_out), .in_0(ID0), .in_1(IN), .out(multiplexer_1_out));
  D_FF_AS #(.Bits(4)) d_ff_as_2 (.Set(1'b0), .D(multiplexer_2_out), .C(CLK), .Clr(~RST), .Q(ID1));  // open: nQ
  Multiplexer #(.Bits(4)) multiplexer_2 (.sel(and_1_out), .in_0(ID1), .in_1(ID0), .out(multiplexer_2_out));
  or or_1 (or_1_out[3], ID1[0], ID1[2]);
  or or_2 (or_1_out[4], ID1[1], ID1[3]);
  Add #(.Bits(7)) add_1 (
    .a({ID1[3:2], or_1_out, ID1[1:0], 1'b0}), .b({3'b000, ID0}), .c_i(1'b0), .s(HEX), .c_o(add_1_c_o));
  // also tied to GND on the sheet: add_1_c_o
endmodule
