// Digital circuit shifter_pwd.dig as structural Verilog
module shifter_pwd (
  input  [3:0] DATA_in,
  input  [15:0] PWD_in,
  input  EN,
  input  DA,
  input  CLK,
  input  RST,
  output MATCH,
  output LED1,
  output LED2,
  output LED3,
  output LED4
);

  wire and_1_out, and_2_out, and_3_out, and_4_out, and_5_out, and_6_out, and_7_out, and_8_out, and_9_out,
       and_10_out, and_11_out, and_12_out, and_13_out, and_14_out, and_15_out, and_16_out, d_ff_as_5_q,
       d_ff_as_6_nq, d_ff_as_6_q, d_ff_as_7_nq, d_ff_as_7_q, or_2_out, or_4_out, xnor_1_out, xnor_2_out,
       xnor_3_out, xnor_4_out, xnor_5_out, xnor_6_out, xnor_7_out, xnor_8_out, xnor_9_out, xnor_10_out,
       xnor_11_out, xnor_12_out, xnor_13_out, xnor_14_out, xnor_15_out, xnor_16_out, xor_1_out;
  wire [3:0] d_ff_as_1_q, d_ff_as_2_q, d_ff_as_3_q, d_ff_as_4_q, multiplexer_1_out, multiplexer_2_out,
       multiplexer_3_out, multiplexer_4_out;

  xnor xnor_1 (xnor_1_out, PWD_in[12], d_ff_as_4_q[0]);
  xnor xnor_2 (xnor_2_out, PWD_in[13], d_ff_as_4_q[1]);
  xnor xnor_3 (xnor_3_out, PWD_in[14], d_ff_as_4_q[2]);
  xnor xnor_4 (xnor_4_out, PWD_in[15], d_ff_as_4_q[3]);
  and and_1 (and_1_out, EN, RST);
  and and_2 (and_2_out, xnor_1_out, xnor_2_out, xnor_3_out, xnor_4_out);
  D_FF_AS #(.Bits(4)) d_ff_as_1 (
    .Set(1'b0), .D(multiplexer_1_out), .C(CLK), .Clr(~and_1_out), .Q(d_ff_as_1_q));  // open: nQ
  Multiplexer #(.Bits(4)) multiplexer_1 (.sel(and_6_out), .in_0(d_ff_as_1_q), .in_1(DATA_in), .out(multiplexer_1_out));
  xnor xnor_5 (xnor_5_out, PWD_in[8], d_ff_as_3_q[0]);
  xnor xnor_6 (xnor_6_out, PWD_in[9], d_ff_as_3_q[1]);
  xnor xnor_7 (xnor_7_out, PWD_in[10], d_ff_as_3_q[2]);
  xnor xnor_8 (xnor_8_out, PWD_in[11], d_ff_as_3_q[3]);
  D_FF_AS #(.Bits(4)) d_ff_as_2 (
    .Set(1'b0), .D(multiplexer_2_out), .C(CLK), .Clr(~and_1_out), .Q(d_ff_as_2_q));  // open: nQ
  Multiplexer #(.Bits(4)) multiplexer_2 (
    .sel(and_6_out), .in_0(d_ff_as_2_q), .in_1(d_ff_as_1_q), .out(multiplexer_2_out));
  and and_3 (and_3_out, xnor_5_out, xnor_6_out, xnor_7_out, xnor_8_out);
  D_FF_AS #(.Bits(4)) d_ff_as_3 (
    .Set(1'b0), .D(multiplexer_3_out), .C(CLK), .Clr(~and_1_out), .Q(d_ff_as_3_q));  // open: nQ
  Multiplexer #(.Bits(4)) multiplexer_3 (
    .sel(and_6_out), .in_0(d_ff_as_3_q), .in_1(d_ff_as_2_q), .out(multiplexer_3_out));
  xnor xnor_9 (xnor_9_out, PWD_in[4], d_ff_as_2_q[0]);
  xnor xnor_10 (xnor_10_out, PWD_in[5], d_ff_as_2_q[1]);
  xnor xnor_11 (xnor_11_out, PWD_in[6], d_ff_as_2_q[2]);
  xnor xnor_12 (xnor_12_out, PWD_in[7], d_ff_as_2_q[3]);
  and and_4 (and_4_out, xnor_9_out, xnor_10_out, xnor_11_out, xnor_12_out);
  D_FF_AS #(.Bits(4)) d_ff_as_4 (
    .Set(1'b0), .D(multiplexer_4_out), .C(CLK), .Clr(~and_1_out), .Q(d_ff_as_4_q));  // open: nQ
  Multiplexer #(.Bits(4)) multiplexer_4 (
    .sel(and_6_out), .in_0(d_ff_as_4_q), .in_1(d_ff_as_3_q), .out(multiplexer_4_out));
  and and_5 (and_5_out, DA, and_1_out);
  D_FF_AS d_ff_as_5 (.Set(1'b0), .D(or_2_out), .C(CLK), .Clr(~and_1_out), .Q(d_ff_as_5_q));  // open: nQ
  D_FF_AS d_ff_as_6 (.Set(1'b0), .D(or_4_out), .C(CLK), .Clr(~and_1_out), .Q(d_ff_as_6_q), .nQ(d_ff_as_6_nq));
  D_FF_AS d_ff_as_7 (.Set(1'b0), .D(xor_1_out), .C(CLK), .Clr(~and_1_out), .Q(d_ff_as_7_q), .nQ(d_ff_as_7_nq));
  and and_6 (and_6_out, and_5_out, ~and_11_out);  // And
  xnor xnor_13 (xnor_13_out, PWD_in[0], d_ff_as_1_q[0]);
  xnor xnor_14 (xnor_14_out, PWD_in[1], d_ff_as_1_q[1]);
  xnor xnor_15 (xnor_15_out, PWD_in[2], d_ff_as_1_q[2]);
  xnor xnor_16 (xnor_16_out, PWD_in[3], d_ff_as_1_q[3]);
  and and_7 (and_7_out, d_ff_as_6_q, d_ff_as_7_q, and_5_out);
  and and_8 (and_8_out, d_ff_as_6_nq, d_ff_as_7_q, and_5_out);
  and and_9 (and_9_out, d_ff_as_6_q, d_ff_as_7_nq);
  and and_10 (and_10_out, d_ff_as_6_q, ~and_5_out);  // And
  xor xor_1 (xor_1_out, d_ff_as_7_q, and_5_out);
  and and_11 (and_11_out, d_ff_as_5_q, and_5_out);
  or or_1 (LED1, d_ff_as_5_q, d_ff_as_6_q, d_ff_as_7_q, and_5_out);
  and and_12 (and_12_out, d_ff_as_7_q, and_5_out);
  and and_13 (and_13_out, d_ff_as_6_q, and_5_out);
  and and_14 (and_14_out, d_ff_as_6_q, d_ff_as_7_q);
  and and_15 (and_15_out, d_ff_as_6_q, d_ff_as_7_q, and_5_out);
  or or_2 (or_2_out, and_7_out, d_ff_as_5_q);
  or or_3 (LED4, and_15_out, d_ff_as_5_q);
  and and_16 (and_16_out, xnor_13_out, xnor_14_out, xnor_15_out, xnor_16_out);
  or or_4 (or_4_out, and_8_out, and_9_out, and_10_out);
  or or_5 (LED2, and_12_out, d_ff_as_5_q, d_ff_as_6_q);
  or or_6 (LED3, and_13_out, and_14_out, d_ff_as_5_q);
  and and_17 (MATCH, and_2_out, and_3_out, and_4_out, and_16_out);
endmodule
