// Digital circuit timer.dig as structural Verilog
module timer (
  input  START,
  input  CLK,
  input  RST,
  output RESET,
  output DIS
);

  wire and_1_out, d_ff_1_q, d_ff_as_1_nq, d_ff_as_1_q, d_ff_as_2_nq, d_ff_as_2_q, d_ff_as_3_nq, d_ff_as_3_q,
       d_ff_as_4_nq, d_ff_as_4_q, d_ff_as_5_nq, d_ff_as_5_q, d_ff_as_6_nq, d_ff_as_6_q, d_ff_as_7_nq,
       d_ff_as_8_nq, d_ff_as_8_q, d_ff_as_9_nq, d_ff_as_9_q;

  and and_1 (and_1_out, START, RST);
  D_FF_AS d_ff_as_1 (
    .Set(1'b0), .D(d_ff_as_1_nq), .C(d_ff_as_9_q), .Clr(~and_1_out), .Q(d_ff_as_1_q), .nQ(d_ff_as_1_nq));
  D_FF_AS d_ff_as_2 (.Set(1'b0), .D(d_ff_as_2_nq), .C(CLK), .Clr(~and_1_out), .Q(d_ff_as_2_q), .nQ(d_ff_as_2_nq));
  D_FF_AS d_ff_as_3 (
    .Set(1'b0), .D(d_ff_as_3_nq), .C(d_ff_as_1_q), .Clr(~and_1_out), .Q(d_ff_as_3_q), .nQ(d_ff_as_3_nq));
  D_FF_AS d_ff_as_4 (
    .Set(1'b0), .D(d_ff_as_4_nq), .C(d_ff_as_2_q), .Clr(~and_1_out), .Q(d_ff_as_4_q), .nQ(d_ff_as_4_nq));
  D_FF_AS d_ff_as_5 (
    .Set(1'b0), .D(d_ff_as_5_nq), .C(d_ff_as_3_q), .Clr(~and_1_out), .Q(d_ff_as_5_q), .nQ(d_ff_as_5_nq));
  D_FF_AS d_ff_as_6 (
    .Set(1'b0), .D(d_ff_as_6_nq), .C(d_ff_as_4_q), .Clr(~and_1_out), .Q(d_ff_as_6_q), .nQ(d_ff_as_6_nq));
  D_FF_AS d_ff_as_7 (.Set(1'b0), .D(d_ff_as_7_nq), .C(d_ff_as_5_q), .Clr(~and_1_out), .Q(DIS), .nQ(d_ff_as_7_nq));
  D_FF_AS d_ff_as_8 (
    .Set(1'b0), .D(d_ff_as_8_nq), .C(d_ff_as_6_q), .Clr(~and_1_out), .Q(d_ff_as_8_q), .nQ(d_ff_as_8_nq));
  D_FF d_ff_1 (.D(DIS), .C(CLK), .Q(d_ff_1_q));  // open: nQ
  D_FF_AS d_ff_as_9 (
    .Set(1'b0), .D(d_ff_as_9_nq), .C(d_ff_as_8_q), .Clr(~and_1_out), .Q(d_ff_as_9_q), .nQ(d_ff_as_9_nq));
  and and_2 (RESET, ~DIS, d_ff_1_q);  // And
endmodule
